// Logisim project LCD_aula.circ as structural Verilog: 1 circuit, main circuit main
module main (
  input  in_1,
  input  in_2
);

  wire clock_1_out, counter_1_carry, undriven;
  wire [4:0] counter_1_q;
  wire [6:0] ram_1_data;

  Clock clock_1 (.out(clock_1_out));
  Counter #(.width(5), .max('h1f)) counter_1 (
    .count(in_1), .Q(counter_1_q), .carry(counter_1_carry), .clk(clock_1_out), .clr(in_2));  // open: load, D
  RAM #(.addrWidth(5), .dataWidth(7)) ram_1 (
    .addr(counter_1_q), .data(ram_1_data), .sel(undriven), .ld(1'b1));  // open: clk, clr
  TTY tty_1 (.data(ram_1_data), .clk(clock_1_out), .clr(counter_1_carry));  // open: we

  // Notes on the sheet:
  //   ASCII
  //   LCD
endmodule
