// Logisim project 2.Contador_PC.circ as structural Verilog: 1 circuit, main circuit main
module main (
  input  in_1,
  input  [3:0] in_2,
  input  in_3,
  input  Clear,
  output [3:0] out_5
);

  wire Clock_out;

  Clock Clock (.out(Clock_out));
  Hex_Digit_Display hex_digit_display_1 (.value(out_5));  // open: dp
  Counter #(.width(4), .max('h9)) counter_1 (
    .load(in_1), .D(in_2), .count(in_3), .Q(out_5), .clk(Clock_out), .clr(Clear));  // open: carry
endmodule
