// Logisim project 4.LCD.circ as structural Verilog: 1 circuit, main circuit main
module main (
  input  in_1
);

  wire clock_1_out, undriven;
  wire [3:0] counter_1_q;
  wire [6:0] ram_1_data;

  Clock clock_1 (.out(clock_1_out));
  Counter #(.width(4), .max('ha)) counter_1 (.Q(counter_1_q), .clk(clock_1_out));  // open: load, D, count, carry, clr
  RAM #(.addrWidth(4), .dataWidth(7)) ram_1 (
    .addr(counter_1_q), .data(ram_1_data), .sel(undriven), .clk(clock_1_out));  // open: ld, clr
  TTY tty_1 (.data(ram_1_data), .clk(clock_1_out), .clr(in_1));  // open: we

  // Notes on the sheet:
  //   ASCII
  //   LCD
endmodule
