// Logisim project LCD_aula.circ as structural Verilog: 1 circuit, main circuit main
module main (
);

  wire undriven;
  wire [4:0] counter_1_q;

  Clock clock_1 ();  // open: out
  Counter #(.width(5), .max('h1f)) counter_1 (.Q(counter_1_q));  // open: load, D, count, carry, clk, clr
  RAM #(.addrWidth(5), .dataWidth(7)) ram_1 (.addr(counter_1_q), .sel(undriven));  // open: data, clk, ld, clr
  TTY tty_1 ();  // open: data, clk, we, clr

  // Notes on the sheet:
  //   ASCII
  //   LCD
endmodule
