// Logisim project Memoria RAM.circ as structural Verilog: 1 circuit, main circuit main
module main (
  input  [3:0] \Endereço ,
  input  [7:0] Dados,
  input  in_3,
  input  in_4,
  input  in_5,
  input  in_6,
  output [7:0] \Saída 
);

  wire clock_1_out;

  Clock clock_1 (.out(clock_1_out));
  Hex_Digit_Display hex_digit_display_1 (.value(\Saída [7:4]));  // open: dp
  RAM #(.addrWidth(4), .bus("separate")) ram_1 (
    .addr(\Endereço ), .din(Dados), .data(\Saída ), .str(in_3), .sel(in_4), .clk(clock_1_out), .ld(in_5),
    .clr(in_6));
  Hex_Digit_Display hex_digit_display_2 (.value(\Saída [3:0]));  // open: dp
endmodule
