// Logisim project Memoria ROM.circ as structural Verilog: 1 circuit, main circuit main
module main (
  input  [3:0] in_1,
  input  in_2,
  input  in_3,
  input  Clear,
  input  Chip_select,
  output [7:0] \Saída 
);

  wire clock_1_out;
  wire [3:0] counter_1_q;

  Hex_Digit_Display hex_digit_display_1 (.value(counter_1_q));  // open: dp
  Counter #(.width(4), .max('hf)) counter_1 (
    .load(in_2), .D(in_1), .count(in_3), .Q(counter_1_q), .clk(clock_1_out), .clr(Clear));  // open: carry
  Clock clock_1 (.out(clock_1_out));
  Hex_Digit_Display hex_digit_display_2 (.value(\Saída [7:4]));  // open: dp
  ROM #(.addrWidth(4)) rom_1 (.addr(counter_1_q), .data(\Saída ), .sel(Chip_select));
  Hex_Digit_Display hex_digit_display_3 (.value(\Saída [3:0]));  // open: dp

  // Notes on the sheet:
  //   contents of rom_1 (hex, n*v repeats v):
  //   11 aa f f0 1 80 55 33 12 13 10 22 64 11 26 99
endmodule
