// Logisim project 1.ALU.circ as structural Verilog: 1 circuit, main circuit main
module main (
  input  Carry_IN,
  input  [3:0] A,
  input  [3:0] B,
  input  [1:0] in_4,
  output [3:0] A_B,
  output CARRY_OUT,
  output out_7,
  output [3:0] out_8,
  output [3:0] out_9
);

  wire [3:0] and_1_out, not_1_out, or_1_out, xor_1_out;

  assign and_1_out = B & A;  // AND_Gate and_1, 4 bits wide
  assign or_1_out = B | A;  // OR_Gate or_1, 4 bits wide
  Multiplexer #(.select(2), .width(4), .enable("false")) multiplexer_1 (
    .in0(and_1_out), .in1(or_1_out), .in2(xor_1_out), .in3(not_1_out), .out(out_9), .sel(in_4));
  assign xor_1_out = B ^ A;  // XOR_Gate xor_1, 4 bits wide
  assign not_1_out = ~A;  // NOT_Gate not_1, 4 bits wide
  Adder #(.width(4)) adder_1 (.a(A), .b(B), .out(A_B), .cin(Carry_IN), .cout(CARRY_OUT));
  Subtractor #(.width(4)) subtractor_1 (.a(A), .b(B), .out(out_8), .bout(out_7));  // open: bin
  Hex_Digit_Display hex_digit_display_1 (.value(A_B));  // open: dp
  Hex_Digit_Display hex_digit_display_2 (.value(out_8));  // open: dp

  // Notes on the sheet:
  //   B
  //   A
endmodule
