// Logisim project 3.CONTROLE.circ as structural Verilog: 1 circuit, main circuit main
module main (
  output [15:0] out_1,
  output [3:0] out_2
);

  wire clock_1_out;

  Counter #(.width(4), .max('hf)) counter_1 (.count(1'b1), .Q(out_2), .clk(clock_1_out));  // open: load, D, carry, clr
  Clock clock_1 (.out(clock_1_out));
  Decoder #(.select(4)) decoder_1 (
    .out0(out_1[0]), .out1(out_1[1]), .out2(out_1[2]), .out3(out_1[3]), .out4(out_1[4]), .out5(out_1[5]),
    .out6(out_1[6]), .out7(out_1[7]), .out8(out_1[8]), .out9(out_1[9]), .out10(out_1[10]), .out11(out_1[11]),
    .out12(out_1[12]), .out13(out_1[13]), .out14(out_1[14]), .out15(out_1[15]), .sel(out_2), .en(1'b1));
endmodule
