// Logisim project 5.Flip_Flop D.circ as structural Verilog: 1 circuit, main circuit main
module main (
  input  CLK,
  input  D,
  input  CLK_2,
  input  D_2,
  input  Preset,
  input  Enable,
  input  Clear,
  output Q,
  output nQ,
  output Q_2,
  output nQ_2
);

  D_Flip_Flop d_ff_1 (.clk(CLK), .D(D), .Q(Q), .Qn(nQ));  // open: preset, en, reset
  D_Flip_Flop d_ff_2 (.clk(CLK_2), .D(D_2), .Q(Q_2), .Qn(nQ_2), .preset(Preset), .en(Enable), .reset(Clear));
endmodule
