// Logisim project CPU.circ as structural Verilog: 1 circuit, main circuit main
module main (
  input  [7:0] in_1,
  input  in_2,
  output [3:0] out_3,
  output [3:0] out_4,
  output out_5,
  output [3:0] out_6,
  output [3:0] out_7,
  output [7:0] out_8
);

  wire _0_out, _1_out, _2_out, _3_out, clock_1_out, clock_2_out, counter_2_carry, d_ff_1_q, decoder_1_out8,
       decoder_1_out15, or_1_out, or_2_out, priority_encoder_1_gs;
  wire [3:0] counter_2_q;
  wire [6:0] multiplexer_1_out, ram_3_data, ram_4_data;

  Button _0 (.out(_0_out));
  Button _2 (.out(_2_out));
  Button _1 (.out(_1_out));
  Button _3 (.out(_3_out));
  Clock clock_1 (.out(clock_1_out));
  Priority_Encoder #(.select(4)) priority_encoder_1 (
    .in0(_0_out), .in1(_1_out), .in2(_2_out), .in3(_3_out), .out(out_3), .gs(priority_encoder_1_gs));  // open: in4, in5, in6, in7, in8, in9, in10, in11, in12, in13, in14, in15, en_out, en_in
  Counter #(.width(4), .max('hf)) counter_1 (.count(in_2), .Q(out_6), .clk(clock_1_out));  // open: load, D, carry, clr
  Hex_Digit_Display hex_digit_display_1 (.value(out_3), .dp(priority_encoder_1_gs));
  RAM #(.addrWidth(4), .dataWidth(4)) ram_1 (.addr(out_6), .data(out_7), .clk(clock_1_out));  // open: sel, ld, clr
  Decoder #(.select(4)) decoder_1 (
    .out0(out_8[0]), .out1(out_8[1]), .out2(out_8[2]), .out3(out_8[3]), .out4(out_8[4]), .out5(out_8[5]),
    .out6(out_8[6]), .out7(out_8[7]), .out8(decoder_1_out8), .out15(decoder_1_out15), .sel(out_7), .en(in_2));  // open: out9, out10, out11, out12, out13, out14
  or or_1 (or_1_out, decoder_1_out15, out_5);
  Counter #(.width(4), .max('h9)) counter_2 (
    .count(in_2), .Q(counter_2_q), .carry(counter_2_carry), .clk(clock_1_out), .clr(or_1_out));  // open: load, D
  RAM #(.dataWidth(4)) ram_2 (.addr(in_1), .data(out_4), .clk(clock_1_out), .ld(1'b1));  // open: sel, clr
  Clock clock_2 (.out(clock_2_out));
  Comparator #(.width(4), .mode("unsigned")) comparator_1 (.a(out_3), .b(out_4), .eq(out_5));  // open: gt, lt
  D_Flip_Flop d_ff_1 (
    .clk(clock_2_out), .D(out_5), .Q(d_ff_1_q), .en(decoder_1_out8), .reset(counter_2_carry));  // open: Qn, preset
  RAM #(.addrWidth(4), .dataWidth(7)) ram_3 (
    .addr(counter_2_q), .data(ram_3_data), .clk(clock_1_out));  // open: sel, ld, clr
  RAM #(.addrWidth(4), .dataWidth(7)) ram_4 (
    .addr(counter_2_q), .data(ram_4_data), .clk(clock_1_out));  // open: sel, ld, clr
  DotMatrix #(.matrixcols(1), .matrixrows(1), .persist(5)) dotmatrix_1 (.col0(d_ff_1_q));
  TTY tty_1 (.data(multiplexer_1_out), .clk(clock_1_out), .clr(or_2_out));  // open: we
  Multiplexer #(.width(7), .disabled(0), .enable("false")) multiplexer_1 (
    .in0(ram_3_data), .in1(ram_4_data), .out(multiplexer_1_out), .sel(d_ff_1_q));
  or or_2 (or_2_out, decoder_1_out15, out_5);

  // Notes on the sheet:
  //   TECLADO
  //   PROGRAMA
  //   CONTROLE
  //   DADOS
  //   PONTEIRO
  //   UNIDADE LÓGICA
  //   ASCII
  //   REGISTROS
  //   LCD
endmodule
