// Logisim project Teclado_Lcd_aula.circ as structural Verilog: 1 circuit, main circuit main
module main (
  input  Clear_LCD,
  output [3:0] out_2
);

  wire _0_out, _1_out, _2_out, _3_out, priority_encoder_1_gs, undriven;

  Button _0 (.out(_0_out));
  Button _2 (.out(_2_out));
  Clock Clock ();  // open: out
  Button _1 (.out(_1_out));
  Button _3 (.out(_3_out));
  Hex_Digit_Display hex_digit_display_1 (.value(out_2), .dp(priority_encoder_1_gs));
  Priority_Encoder #(.select(4)) priority_encoder_1 (
    .in0(_0_out), .in1(_1_out), .in2(_2_out), .in3(_3_out), .out(out_2), .gs(priority_encoder_1_gs));  // open: in4, in5, in6, in7, in8, in9, in10, in11, in12, in13, in14, in15, en_out, en_in
  RAM #(.addrWidth(4), .dataWidth(7)) ram_1 (.sel(undriven));  // open: addr, data, clk, ld, clr
  TTY tty_1 ();  // open: data, clk, we, clr

  // Notes on the sheet:
  //   ASCII
  //   LCD
endmodule
