// Logisim project Circuito-de-7-Segmentos.circ as structural Verilog: 2 circuits, main circuit main
module main (
  input  v_Reverso,
  input  in_2
);

  wire and_1_out, button_1_out, ci_circuitosegmentos_1_l1, ci_circuitosegmentos_1_l2,
       ci_circuitosegmentos_1_l3, ci_circuitosegmentos_1_l4, ci_circuitosegmentos_1_l5,
       ci_circuitosegmentos_1_l6, ci_circuitosegmentos_1_l7, clock_1_out, or_1_out;
  wire [3:0] counter_1_q;

  Button button_1 (.out(button_1_out));
  Clock clock_1 (.out(clock_1_out));
  or or_1 (or_1_out, button_1_out, and_1_out);
  and and_1 (and_1_out, clock_1_out, in_2);
  Counter #(.width(4), .max('hf)) counter_1 (
    .load(v_Reverso), .Q(counter_1_q), .clk(or_1_out));  // open: D, count, carry, clr
  CI_CircuitoSegmentos ci_circuitosegmentos_1 (
    .D3(counter_1_q[3]), .D2(counter_1_q[2]), .D1(counter_1_q[1]), .D0(counter_1_q[0]),
    .L1(ci_circuitosegmentos_1_l1), .L2(ci_circuitosegmentos_1_l2), .L3(ci_circuitosegmentos_1_l3),
    .L4(ci_circuitosegmentos_1_l4), .L5(ci_circuitosegmentos_1_l5), .L6(ci_circuitosegmentos_1_l6),
    .L7(ci_circuitosegmentos_1_l7));
  _7_Segment_Display u_7_segment_display_1 (
    .g(ci_circuitosegmentos_1_l2), .f(ci_circuitosegmentos_1_l4), .a(ci_circuitosegmentos_1_l1),
    .b(ci_circuitosegmentos_1_l6), .e(ci_circuitosegmentos_1_l5), .d(ci_circuitosegmentos_1_l3),
    .c(ci_circuitosegmentos_1_l7));  // open: dp

  // Notes on the sheet:
  //   v Manual
  //   ^  Automâtico   
endmodule

module CI_CircuitoSegmentos (
  input  D3,
  input  D2,
  input  D1,
  input  D0,
  output L1,
  output L2,
  output L3,
  output L4,
  output L5,
  output L6,
  output L7
);

  wire and_1_out, and_2_out, and_3_out, and_4_out, and_5_out, and_6_out, and_7_out, and_8_out, and_9_out,
       and_10_out, and_11_out, and_12_out, and_13_out, and_14_out, and_15_out, and_16_out, and_17_out,
       and_18_out, and_19_out, and_20_out, and_21_out, not_1_out, not_2_out, not_3_out, not_4_out, not_5_out,
       not_6_out, not_7_out, not_8_out, not_9_out, not_10_out, not_11_out, not_12_out, not_13_out,
       not_14_out, not_15_out, not_16_out, not_17_out, not_18_out, not_19_out, not_20_out, not_21_out,
       not_22_out, not_23_out, not_24_out, not_25_out, not_26_out, not_27_out, not_28_out, not_29_out;

  not not_1 (not_1_out, D3);
  not not_2 (not_2_out, D0);
  not not_3 (not_3_out, D1);
  not not_4 (not_4_out, D2);
  not not_5 (not_5_out, D3);
  and and_1 (and_1_out, not_5_out, not_6_out);
  not not_6 (not_6_out, D1);
  not not_7 (not_7_out, D3);
  and and_2 (and_2_out, not_7_out, D0);
  and and_3 (and_3_out, D2, D0);
  not not_8 (not_8_out, D2);
  and and_4 (and_4_out, not_8_out, not_9_out, D0);
  not not_9 (not_9_out, D1);
  not not_10 (not_10_out, D3);
  and and_5 (and_5_out, not_10_out, not_11_out, D1);
  not not_11 (not_11_out, D2);
  and and_6 (and_6_out, D1, not_12_out);
  not not_12 (not_12_out, D0);
  and and_7 (and_7_out, D2, not_13_out);
  not not_13 (not_13_out, D0);
  and and_8 (and_8_out, D3, D2, D1);
  not not_14 (not_14_out, D3);
  and and_9 (and_9_out, not_14_out, not_15_out);
  not not_15 (not_15_out, D1);
  not not_16 (not_16_out, D0);
  and and_10 (and_10_out, D3, D1);
  not not_17 (not_17_out, D3);
  not not_18 (not_18_out, D2);
  not not_19 (not_19_out, D1);
  not not_20 (not_20_out, D0);
  not not_21 (not_21_out, D3);
  not not_22 (not_22_out, D2);
  not not_23 (not_23_out, D1);
  not not_24 (not_24_out, D0);
  not not_25 (not_25_out, D3);
  and and_11 (and_11_out, not_25_out, not_26_out, not_27_out);
  not not_26 (not_26_out, D2);
  not not_27 (not_27_out, D1);
  not not_28 (not_28_out, D2);
  and and_12 (and_12_out, not_28_out, D0);
  and and_13 (and_13_out, D2, D1);
  and and_14 (and_14_out, D3, D2, not_29_out);
  not not_29 (not_29_out, D0);
  and and_15 (and_15_out, not_1_out, not_2_out);
  and and_16 (and_16_out, D2, not_3_out);
  or or_1 (L1, and_15_out, and_16_out, and_17_out);
  and and_17 (and_17_out, D3, not_4_out, D1, D0);
  or or_2 (L2, and_1_out, and_2_out, and_3_out);
  or or_3 (L3, and_4_out, and_5_out, and_6_out, and_7_out, and_8_out);
  or or_4 (L4, and_9_out, not_16_out, D2, and_10_out);
  or or_5 (L5, not_17_out, not_18_out, not_19_out, not_20_out);
  and and_18 (and_18_out, not_21_out, not_22_out, not_23_out, not_24_out);
  and and_19 (and_19_out, D1, D0);
  and and_20 (and_20_out, D3, D0);
  and and_21 (and_21_out, D3, D2);
  or or_6 (L7, and_11_out, and_12_out, and_13_out, and_14_out);
  or or_7 (L6, and_18_out, and_19_out, and_20_out, and_21_out);
endmodule
