// Logisim project mem4x4.circ as structural Verilog: 9 circuits, main circuit Memória 4x4
module teste_memoria_4x4 (
  input  [1:0] \endereço ,
  input  [3:0] dados_in,
  input  W_R_prime,
  input  CE,
  output [3:0] dados_out
);

  \Memória_4x4  \memória_4x4_1  (
    .A1(\endereço [0]), .A0(\endereço [1]), .WR_prime(W_R_prime), .CE(CE), .S3(dados_out[0]),
    .S2(dados_out[1]), .S1(dados_out[2]), .S0(dados_out[3]), .in_5(dados_in[0]), .in_6(dados_in[1]),
    .in_7(dados_in[2]), .in_8(dados_in[3]));

  // Notes on the sheet:
  //   Operação:
  //   A1A0
  //   ///////////
  //   W/R'
  //   CE
  //   dados_out
  //   Escrita
  //   A1A0
  //   ///////////
  //   W/R'
  //   CE
  //   dados_in
  //   //////
  //   Leitura (observar a ordem dos sinais)
  //   --------------------  ------------------  -----------------
  //   end
  //   X
  //   X
  //   --------------------  ------------------  -----------------
  //   ----------------------------------------------------------
  //   -----------
  //   \
  //   /
  //   --------------------                   -----------------
  //   --------------------------   -------------  --------------------
  //   dado
  //      X
  //   /////////////
  //   X
  //   ---------------------------  ------------  ----------------------
  //   --------------------  ------------------  -----------------
  //   end
  //   X
  //   X
  //   --------------------  ------------------  -----------------
  //   ------------
  //   /
  //   \
  //   --------------------                   -----------------
  //   -----------
  //   /
  //   \
  //   --------------------                   -----------------
  //   -------------------   ---------------------  --------------------
  //   dado
  //   X
  //      X
  //   -------------------   ---------------------   ----------------------
  //   /////////////
  //   /////////////
  //   /////////////
  //   /////////////
endmodule

module \Memória_4x4  (
  input  A1,
  input  A0,
  input  WR_prime,
  input  CE,
  input  in_5,
  input  in_6,
  input  in_7,
  input  in_8,
  output S3,
  output S2,
  output S1,
  output S0
);

  wire and_1_out, and_2_out, buffer_1_out, buffer_2_out, buffer_3_out, buffer_4_out, celulabasica_1_output,
       celulabasica_2_output, celulabasica_9_output, celulabasica_13_output, decodificador_2x4_1_d0,
       decodificador_2x4_1_d1, decodificador_2x4_1_d2, decodificador_2x4_1_d3;

  Decodificador_2x4 decodificador_2x4_1 (
    .A1(A1), .A0(A0), .D0(decodificador_2x4_1_d0), .D1(decodificador_2x4_1_d1), .D2(decodificador_2x4_1_d2),
    .D3(decodificador_2x4_1_d3));
  and and_1 (and_1_out, WR_prime, CE);
  and and_2 (and_2_out, CE, ~WR_prime);  // AND_Gate
  buf buffer_1 (buffer_1_out, in_5);
  CelulaBasica celulabasica_1 (
    .Cell_Enable(decodificador_2x4_1_d0), .Input(buffer_2_out), .Write_Enable(and_1_out),
    .Output(celulabasica_1_output));
  CelulaBasica celulabasica_2 (
    .Cell_Enable(decodificador_2x4_1_d0), .Input(buffer_1_out), .Write_Enable(and_1_out),
    .Output(celulabasica_2_output));
  CelulaBasica celulabasica_3 (
    .Cell_Enable(decodificador_2x4_1_d1), .Input(buffer_1_out), .Write_Enable(and_1_out),
    .Output(celulabasica_2_output));
  CelulaBasica celulabasica_4 (
    .Cell_Enable(decodificador_2x4_1_d1), .Input(buffer_2_out), .Write_Enable(and_1_out),
    .Output(celulabasica_1_output));
  CelulaBasica celulabasica_5 (
    .Cell_Enable(decodificador_2x4_1_d2), .Input(buffer_1_out), .Write_Enable(and_1_out),
    .Output(celulabasica_2_output));
  CelulaBasica celulabasica_6 (
    .Cell_Enable(decodificador_2x4_1_d2), .Input(buffer_2_out), .Write_Enable(and_1_out),
    .Output(celulabasica_1_output));
  CelulaBasica celulabasica_7 (
    .Cell_Enable(decodificador_2x4_1_d3), .Input(buffer_2_out), .Write_Enable(and_1_out),
    .Output(celulabasica_1_output));
  CelulaBasica celulabasica_8 (
    .Cell_Enable(decodificador_2x4_1_d3), .Input(buffer_1_out), .Write_Enable(and_1_out),
    .Output(celulabasica_2_output));
  buf buffer_2 (buffer_2_out, in_6);
  assign in_5 = and_2_out ? celulabasica_2_output : 1'bz;  // Controlled_Buffer controlled_buffer_1
  CelulaBasica celulabasica_9 (
    .Cell_Enable(decodificador_2x4_1_d0), .Input(buffer_3_out), .Write_Enable(and_1_out),
    .Output(celulabasica_9_output));
  CelulaBasica celulabasica_10 (
    .Cell_Enable(decodificador_2x4_1_d1), .Input(buffer_3_out), .Write_Enable(and_1_out),
    .Output(celulabasica_9_output));
  CelulaBasica celulabasica_11 (
    .Cell_Enable(decodificador_2x4_1_d2), .Input(buffer_3_out), .Write_Enable(and_1_out),
    .Output(celulabasica_9_output));
  CelulaBasica celulabasica_12 (
    .Cell_Enable(decodificador_2x4_1_d3), .Input(buffer_3_out), .Write_Enable(and_1_out),
    .Output(celulabasica_9_output));
  buf buffer_3 (buffer_3_out, in_7);
  assign in_6 = and_2_out ? celulabasica_1_output : 1'bz;  // Controlled_Buffer controlled_buffer_2
  assign in_7 = and_2_out ? celulabasica_9_output : 1'bz;  // Controlled_Buffer controlled_buffer_3
  CelulaBasica celulabasica_13 (
    .Cell_Enable(decodificador_2x4_1_d0), .Input(buffer_4_out), .Write_Enable(and_1_out),
    .Output(celulabasica_13_output));
  CelulaBasica celulabasica_14 (
    .Cell_Enable(decodificador_2x4_1_d1), .Input(buffer_4_out), .Write_Enable(and_1_out),
    .Output(celulabasica_13_output));
  CelulaBasica celulabasica_15 (
    .Cell_Enable(decodificador_2x4_1_d2), .Input(buffer_4_out), .Write_Enable(and_1_out),
    .Output(celulabasica_13_output));
  CelulaBasica celulabasica_16 (
    .Cell_Enable(decodificador_2x4_1_d3), .Input(buffer_4_out), .Write_Enable(and_1_out),
    .Output(celulabasica_13_output));
  buf buffer_4 (buffer_4_out, in_8);
  assign in_8 = and_2_out ? celulabasica_13_output : 1'bz;  // Controlled_Buffer controlled_buffer_4

  assign S0 = in_8;
  assign S1 = in_7;
  assign S2 = in_6;
  assign S3 = in_5;
endmodule

// MC
module CelulaBasica (
  input  Cell_Enable,
  input  Input,
  input  Write_Enable,
  output Output
);

  wire and_1_out, d_ff_1_q;

  and and_1 (and_1_out, Cell_Enable, Write_Enable);
  D_Flip_Flop #(.trigger("high")) d_ff_1 (.clk(and_1_out), .D(Input), .Q(d_ff_1_q));  // open: Qn, preset, en, reset
  assign Output = Cell_Enable ? d_ff_1_q : 1'bz;  // Controlled_Buffer controlled_buffer_1
endmodule

module Decodificador_3x8 (
  input  A2,
  input  A1,
  input  A0,
  output D0,
  output D1,
  output D2,
  output D3,
  output D4,
  output D5,
  output D6,
  output D8
);

  and and_1 (D0, ~A0, ~A1, ~A2);  // AND_Gate
  and and_2 (D1, A0, ~A1, ~A2);  // AND_Gate
  and and_3 (D2, ~A0, A1, ~A2);  // AND_Gate
  and and_4 (D3, A0, A1, ~A2);  // AND_Gate
  and and_5 (D4, ~A0, ~A1, A2);  // AND_Gate
  and and_6 (D5, A0, ~A1, A2);  // AND_Gate
  and and_7 (D6, ~A0, A1, A2);  // AND_Gate
  and and_8 (D8, A0, A1, A2);
endmodule

module Decodificador_2x4 (
  input  A1,
  input  A0,
  output D0,
  output D1,
  output D2,
  output D3
);

  and and_1 (D0, ~A1, ~A0);  // AND_Gate
  and and_2 (D1, A0, ~A1);  // AND_Gate
  and and_3 (D2, ~A0, A1);  // AND_Gate
  and and_4 (D3, A0, A1);
endmodule

module \memória_4x8  (
  input  A0,
  input  A1,
  input  W_R_prime,
  input  CE,
  input  in_5,
  input  in_6,
  input  in_7,
  input  in_8,
  input  in_9,
  input  in_10,
  input  in_11,
  input  in_12,
  output out_13,
  output out_14,
  output out_15,
  output out_16,
  output out_17,
  output out_18,
  output out_19,
  output out_20
);

  \Memória_4x4  \memória_4x4_1  (
    .A1(A0), .A0(A1), .WR_prime(W_R_prime), .CE(CE), .S3(out_13), .S2(out_14), .S1(out_15), .S0(out_16),
    .in_5(in_5), .in_6(in_6), .in_7(in_7), .in_8(in_8));
  \Memória_4x4  \memória_4x4_2  (
    .A1(A0), .A0(A1), .WR_prime(W_R_prime), .CE(CE), .S3(out_17), .S2(out_18), .S1(out_19), .S0(out_20),
    .in_5(in_9), .in_6(in_10), .in_7(in_11), .in_8(in_12));
endmodule

module teste_4x8 (
  input  in_1,
  input  in_2,
  input  in_3,
  input  in_4,
  input  [7:0] in_5,
  output [7:0] out_6
);

  \memória_4x8  \memória_4x8_1  (
    .A0(in_1), .A1(in_2), .W_R_prime(in_3), .CE(in_4), .out_13(out_6[0]), .out_14(out_6[1]),
    .out_15(out_6[2]), .out_16(out_6[3]), .out_17(out_6[4]), .out_18(out_6[5]), .out_19(out_6[6]),
    .out_20(out_6[7]), .in_5(in_5[0]), .in_6(in_5[1]), .in_7(in_5[2]), .in_8(in_5[3]), .in_9(in_5[4]),
    .in_10(in_5[5]), .in_11(in_5[6]), .in_12(in_5[7]));
endmodule

module mem_16x8 (
  input  in_1,
  input  in_2,
  input  in_3,
  input  in_4,
  input  in_5,
  input  in_6,
  input  [7:0] in_7,
  output [7:0] out_8
);

  wire and_1_out, and_2_out, and_3_out, and_4_out, decodificador_2x4_1_d0, decodificador_2x4_1_d1,
       decodificador_2x4_1_d2, decodificador_2x4_1_d3;

  Decodificador_2x4 decodificador_2x4_1 (
    .A1(in_3), .A0(in_4), .D0(decodificador_2x4_1_d0), .D1(decodificador_2x4_1_d1),
    .D2(decodificador_2x4_1_d2), .D3(decodificador_2x4_1_d3));
  and and_1 (and_1_out, decodificador_2x4_1_d0, in_5);
  and and_2 (and_2_out, decodificador_2x4_1_d1, in_5);
  and and_3 (and_3_out, decodificador_2x4_1_d2, in_5);
  and and_4 (and_4_out, decodificador_2x4_1_d3, in_5);
  \memória_4x8  \memória_4x8_1  (
    .A0(in_1), .A1(in_2), .W_R_prime(in_6), .CE(and_1_out), .out_13(out_8[0]), .out_14(out_8[1]),
    .out_15(out_8[2]), .out_16(out_8[3]), .out_17(out_8[4]), .out_18(out_8[5]), .out_19(out_8[6]),
    .out_20(out_8[7]), .in_5(in_7[0]), .in_6(in_7[1]), .in_7(in_7[2]), .in_8(in_7[3]), .in_9(in_7[4]),
    .in_10(in_7[5]), .in_11(in_7[6]), .in_12(in_7[7]));
  \memória_4x8  \memória_4x8_2  (
    .A0(in_1), .A1(in_2), .W_R_prime(in_6), .CE(and_2_out), .out_13(out_8[0]), .out_14(out_8[1]),
    .out_15(out_8[2]), .out_16(out_8[3]), .out_17(out_8[4]), .out_18(out_8[5]), .out_19(out_8[6]),
    .out_20(out_8[7]), .in_5(in_7[0]), .in_6(in_7[1]), .in_7(in_7[2]), .in_8(in_7[3]), .in_9(in_7[4]),
    .in_10(in_7[5]), .in_11(in_7[6]), .in_12(in_7[7]));
  \memória_4x8  \memória_4x8_3  (
    .A0(in_1), .A1(in_2), .W_R_prime(in_6), .CE(and_3_out), .out_13(out_8[0]), .out_14(out_8[1]),
    .out_15(out_8[2]), .out_16(out_8[3]), .out_17(out_8[4]), .out_18(out_8[5]), .out_19(out_8[6]),
    .out_20(out_8[7]), .in_5(in_7[0]), .in_6(in_7[1]), .in_7(in_7[2]), .in_8(in_7[3]), .in_9(in_7[4]),
    .in_10(in_7[5]), .in_11(in_7[6]), .in_12(in_7[7]));
  \memória_4x8  \memória_4x8_4  (
    .A0(in_1), .A1(in_2), .W_R_prime(in_6), .CE(and_4_out), .out_13(out_8[0]), .out_14(out_8[1]),
    .out_15(out_8[2]), .out_16(out_8[3]), .out_17(out_8[4]), .out_18(out_8[5]), .out_19(out_8[6]),
    .out_20(out_8[7]), .in_5(in_7[0]), .in_6(in_7[1]), .in_7(in_7[2]), .in_8(in_7[3]), .in_9(in_7[4]),
    .in_10(in_7[5]), .in_11(in_7[6]), .in_12(in_7[7]));
endmodule

module test_16x8 (
  input  [3:0] in_1,
  input  in_2,
  input  [7:0] in_3,
  input  in_4,
  output [7:0] out_5
);

  mem_16x8 mem_16x8_1 (
    .in_1(in_1[0]), .in_2(in_1[1]), .in_3(in_1[2]), .in_4(in_1[3]), .in_5(in_4), .in_6(in_2), .out_8(out_5),
    .in_7(in_3));
endmodule
