// Logisim project relógio digital.circ as structural Verilog: 4 circuits, main circuit main
module main (
  input  reset
);

  wire _0_a59_clk_seguinte, _0_a_59_clk_seguinte, clock_1_out;
  wire [3:0] _0_a59_dezena, _0_a59_unidade, _0_a_23_dezena, _0_a_23_unidade, _0_a_59_dezena, _0_a_59_unidade;

  Hex_Digit_Display hex_digit_display_1 (.value(_0_a_23_unidade));  // open: dp
  Hex_Digit_Display hex_digit_display_2 (.value(_0_a_23_dezena));  // open: dp
  cont_0_a_23 _0_a_23 (
    .reset(reset), .dezena(_0_a_23_dezena), .unidade(_0_a_23_unidade), .CLK(_0_a_59_clk_seguinte));  // open: CLK_seguinte
  Hex_Digit_Display hex_digit_display_3 (.value(_0_a_59_unidade));  // open: dp
  Hex_Digit_Display hex_digit_display_4 (.value(_0_a_59_dezena));  // open: dp
  cont_0_a_59 _0_a_59 (
    .CLK_seguinte(_0_a_59_clk_seguinte), .reset(reset), .dezena(_0_a_59_dezena), .unidade(_0_a_59_unidade),
    .CLK(_0_a59_clk_seguinte));
  Hex_Digit_Display hex_digit_display_5 (.value(_0_a59_dezena));  // open: dp
  Hex_Digit_Display hex_digit_display_6 (.value(_0_a59_unidade));  // open: dp
  cont_0_a_59 _0_a59 (
    .CLK_seguinte(_0_a59_clk_seguinte), .reset(reset), .dezena(_0_a59_dezena), .unidade(_0_a59_unidade),
    .CLK(clock_1_out));
  Clock clock_1 (.out(clock_1_out));
endmodule

module cont_0_a_9 (
  input  CLK,
  input  reset,
  output [3:0] saida,
  output CLK_seguinte
);

  wire or_1_out;
  wire [3:0] adder_1_out;

  Hex_Digit_Display hex_digit_display_1 (.value(saida));  // open: dp
  Register #(.width(4)) register_1 (.D(adder_1_out), .Q(saida), .clk(CLK), .clr(or_1_out));  // open: en
  or or_1 (or_1_out, CLK_seguinte, reset);
  Adder #(.width(4)) adder_1 (.a(saida), .b(4'b0001), .out(adder_1_out));  // open: cin, cout
  nor nor_1 (CLK_seguinte, saida[0], ~saida[1], saida[2], ~saida[3]);  // NOR_Gate
endmodule

module cont_0_a_59 (
  input  CLK,
  input  reset,
  output [3:0] dezena,
  output [3:0] unidade,
  output CLK_seguinte
);

  wire _0a9_2_clk_seguinte, or_1_out;

  Hex_Digit_Display hex_digit_display_1 (.value(dezena));  // open: dp
  cont_0_a_9 _0a9 (.CLK(_0a9_2_clk_seguinte), .reset(or_1_out), .saida(dezena));  // open: CLK_seguinte
  nor nor_1 (CLK_seguinte, dezena[3], ~dezena[2], ~dezena[1], dezena[0], unidade[3], unidade[2], unidade[1], unidade[0]);  // NOR_Gate
  Hex_Digit_Display hex_digit_display_2 (.value(unidade));  // open: dp
  cont_0_a_9 _0a9_2 (.CLK(CLK), .reset(or_1_out), .saida(unidade), .CLK_seguinte(_0a9_2_clk_seguinte));
  or or_1 (or_1_out, CLK_seguinte, reset);
endmodule

module cont_0_a_23 (
  input  CLK,
  input  reset,
  output [3:0] dezena,
  output [3:0] unidade,
  output CLK_seguinte
);

  wire _0a9_2_clk_seguinte, or_1_out;

  Hex_Digit_Display hex_digit_display_1 (.value(dezena));  // open: dp
  cont_0_a_9 _0a9 (.CLK(_0a9_2_clk_seguinte), .reset(or_1_out), .saida(dezena));  // open: CLK_seguinte
  nor nor_1 (CLK_seguinte, dezena[3], dezena[2], ~dezena[1], dezena[0], unidade[3], ~unidade[2], unidade[1], unidade[0]);  // NOR_Gate
  Hex_Digit_Display hex_digit_display_2 (.value(unidade));  // open: dp
  cont_0_a_9 _0a9_2 (.CLK(CLK), .reset(or_1_out), .saida(unidade), .CLK_seguinte(_0a9_2_clk_seguinte));
  or or_1 (or_1_out, CLK_seguinte, reset);
endmodule
