// Logisim project sequencia com flip flop tipo T.circ as structural Verilog: 2 circuits, main circuit main
module main (
  input  CLK,
  input  clear,
  input  enable,
  output out_4,
  output out_5,
  output out_6,
  output out_7
);

  wire controle_1_d0, controle_1_d1, controle_1_d2, controle_1_d3;

  T_Flip_Flop t_ff_1 (.clk(CLK), .T(controle_1_d3), .Q(out_4), .reset(clear), .en(enable));  // open: Qn, preset
  T_Flip_Flop t_ff_2 (.clk(CLK), .T(controle_1_d2), .Q(out_5), .reset(clear), .en(enable));  // open: Qn, preset
  T_Flip_Flop t_ff_3 (.clk(CLK), .T(controle_1_d1), .Q(out_6), .reset(clear), .en(enable));  // open: Qn, preset
  controle controle_1 (
    .Q3(out_4), .Q2(out_5), .Q1(out_6), .Q0(out_7), .D3(controle_1_d3), .D2(controle_1_d2),
    .D1(controle_1_d1), .D0(controle_1_d0));
  T_Flip_Flop t_ff_4 (.clk(CLK), .T(controle_1_d0), .Q(out_7), .reset(clear), .en(enable));  // open: Qn, preset
  Hex_Digit_Display hex_digit_display_1 (.value({out_4, out_5, out_6, out_7}));  // open: dp
endmodule

module controle (
  input  Q3,
  input  Q2,
  input  Q1,
  input  Q0,
  output D3,
  output D2,
  output D1,
  output D0
);

  and and_1 (D3, Q2, Q1, Q0);
  and and_2 (D2, Q1, Q0);

  assign D0 = 1'b1;
  assign D1 = Q0;
endmodule
