// Logisim project trabalho m3.circ as structural Verilog: 5 circuits, main circuit main
module main (
  input  CLK,
  input  clear
);

  wire comparator_1_eq, multiplexer_1_out, sequencia_guilherme_1_clk_comparador,
       sequencia_mariana_1_clk_comparador, t_ff_1_q;
  wire [3:0] multiplexer_2_out, sequencia_guilherme_1_q0, sequencia_mariana_1_q0;

  sequencia_mariana sequencia_mariana_1 (
    .CLK(CLK), .clear(clear), .clk_comparador(sequencia_mariana_1_clk_comparador),
    .Q3(sequencia_mariana_1_q0[3]), .Q2(sequencia_mariana_1_q0[2]), .Q1(sequencia_mariana_1_q0[1]),
    .Q0(sequencia_mariana_1_q0[0]));
  sequencia_guilherme sequencia_guilherme_1 (
    .CLK(CLK), .clear(clear), .clk_comparador(sequencia_guilherme_1_clk_comparador),
    .Q3(sequencia_guilherme_1_q0[3]), .Q2(sequencia_guilherme_1_q0[2]), .Q1(sequencia_guilherme_1_q0[1]),
    .Q0(sequencia_guilherme_1_q0[0]));
  Multiplexer multiplexer_1 (
    .in0(sequencia_guilherme_1_clk_comparador), .in1(sequencia_mariana_1_clk_comparador),
    .out(multiplexer_1_out), .sel(sequencia_mariana_1_clk_comparador));  // open: en
  Comparator #(.width(1)) comparator_1 (.a(multiplexer_1_out), .b(1'b0), .eq(comparator_1_eq));  // open: gt, lt
  Multiplexer #(.width(4)) multiplexer_2 (
    .in0(sequencia_mariana_1_q0), .in1(sequencia_guilherme_1_q0), .out(multiplexer_2_out), .sel(t_ff_1_q));  // open: en
  T_Flip_Flop t_ff_1 (.clk(comparator_1_eq), .T(1'b1), .Q(t_ff_1_q));  // open: Qn, preset, reset, en
  Hex_Digit_Display hex_digit_display_1 (.value(multiplexer_2_out));  // open: dp

  // Notes on the sheet:
  //   Nome
  //   Mariana Ferreira
  //   Guilherme Luiz
  //   sequência
  //   7-11-13-14-4-9-3-12-10-6
  //   15-5-11-6-7-2-1-13-4-10
endmodule

module controle1 (
  input  Q3,
  input  Q2,
  input  Q1,
  input  Q0,
  output D3,
  output D2,
  output D1,
  output D0
);

  wire and_1_out, and_2_out, and_3_out, and_4_out, and_5_out, and_6_out, and_7_out, and_8_out, and_9_out,
       and_10_out, and_11_out, and_12_out, and_13_out, and_14_out, and_15_out, and_16_out, and_17_out,
       and_18_out, not_1_out, not_2_out, not_3_out, not_4_out, not_5_out, not_6_out, not_7_out, not_8_out,
       not_9_out, not_10_out, not_11_out, not_12_out, not_13_out, not_14_out, not_15_out, not_16_out,
       not_17_out, not_18_out, not_19_out, not_20_out, not_21_out, not_22_out, not_23_out;

  not not_1 (not_1_out, Q3);
  and and_1 (and_1_out, not_1_out, Q1, Q0);
  not not_2 (not_2_out, Q2);
  and and_2 (and_2_out, not_2_out, Q1, Q0);
  not not_3 (not_3_out, Q1);
  and and_3 (and_3_out, Q2, not_3_out, not_4_out);
  not not_4 (not_4_out, Q0);
  and and_4 (and_4_out, Q3, Q2, not_5_out);
  not not_5 (not_5_out, Q1);
  not not_6 (not_6_out, Q3);
  and and_5 (and_5_out, not_6_out, not_7_out);
  not not_7 (not_7_out, Q2);
  not not_8 (not_8_out, Q2);
  and and_6 (and_6_out, not_8_out, not_9_out);
  not not_9 (not_9_out, Q0);
  and and_7 (and_7_out, Q1, not_10_out);
  not not_10 (not_10_out, Q0);
  not not_11 (not_11_out, Q1);
  and and_8 (and_8_out, Q2, not_11_out, Q0);
  and and_9 (and_9_out, Q3, Q1);
  not not_12 (not_12_out, Q2);
  and and_10 (and_10_out, not_12_out, not_13_out);
  not not_13 (not_13_out, Q1);
  not not_14 (not_14_out, Q2);
  and and_11 (and_11_out, not_14_out, not_15_out);
  not not_15 (not_15_out, Q0);
  not not_16 (not_16_out, Q3);
  and and_12 (and_12_out, not_16_out, Q1, not_17_out);
  not not_17 (not_17_out, Q0);
  and and_13 (and_13_out, Q2, Q0);
  and and_14 (and_14_out, Q3, not_18_out);
  not not_18 (not_18_out, Q1);
  not not_19 (not_19_out, Q3);
  and and_15 (and_15_out, not_19_out, not_20_out);
  not not_20 (not_20_out, Q0);
  not not_21 (not_21_out, Q2);
  and and_16 (and_16_out, not_21_out, not_22_out);
  not not_22 (not_22_out, Q1);
  not not_23 (not_23_out, Q3);
  and and_17 (and_17_out, not_23_out, Q2);
  and and_18 (and_18_out, Q3, Q1, Q0);
  or or_1 (D3, and_1_out, and_2_out, and_3_out, and_4_out);
  or or_2 (D2, and_5_out, and_6_out, and_7_out, and_8_out, and_9_out);
  or or_3 (D1, and_10_out, and_11_out, and_12_out, and_13_out, and_14_out);
  or or_4 (D0, and_15_out, and_16_out, and_17_out, and_18_out);

  // Notes on the sheet:
  //   7-11-13-14-4-9-3-12-10-6
endmodule

module sequencia_mariana (
  input  CLK,
  input  clear,
  output Q3,
  output Q2,
  output Q1,
  output Q0,
  output clk_comparador
);

  wire controle1_1_d0, controle1_1_d1, controle1_1_d2, controle1_1_d3;

  D_Flip_Flop d_ff_1 (.clk(CLK), .D(controle1_1_d3), .Q(Q3), .reset(clear));  // open: Qn, preset, en
  D_Flip_Flop d_ff_2 (.clk(CLK), .D(controle1_1_d2), .Q(Q2), .reset(clear));  // open: Qn, preset, en
  D_Flip_Flop d_ff_3 (.clk(CLK), .D(controle1_1_d1), .Q(Q1), .reset(clear));  // open: Qn, preset, en
  D_Flip_Flop d_ff_4 (.clk(CLK), .D(controle1_1_d0), .Q(Q0), .reset(clear));  // open: Qn, preset, en
  controle1 controle1_1 (
    .Q3(Q3), .Q2(Q2), .Q1(Q1), .Q0(Q0), .D3(controle1_1_d3), .D2(controle1_1_d2), .D1(controle1_1_d1),
    .D0(controle1_1_d0));
  Hex_Digit_Display hex_digit_display_1 (.value({Q3, Q2, Q1, Q0}));  // open: dp
  nor nor_1 (clk_comparador, Q3, ~Q2, ~Q1, Q0);  // NOR_Gate

  // Notes on the sheet:
  //   7-11-13-14-4-9-3-12-10-6
endmodule

module controle2 (
  input  Q3,
  input  Q2,
  input  Q1,
  input  Q0,
  output D3,
  output D2,
  output D1,
  output D0
);

  wire and_1_out, and_2_out, and_3_out, and_4_out, and_5_out, and_6_out, and_7_out, and_8_out, and_9_out,
       and_10_out, and_11_out, and_12_out, and_13_out, and_14_out, and_15_out, and_16_out, and_17_out,
       and_18_out, not_1_out, not_2_out, not_3_out, not_4_out, not_5_out, not_6_out, not_7_out, not_8_out,
       not_9_out, not_10_out, not_11_out, not_12_out, not_13_out, not_14_out, not_15_out, not_16_out,
       not_17_out, not_18_out, not_19_out, not_20_out, not_21_out, not_22_out, not_23_out, not_24_out,
       not_25_out;

  not not_1 (not_1_out, Q3);
  and and_1 (and_1_out, not_1_out, not_2_out);
  not not_2 (not_2_out, Q1);
  not not_3 (not_3_out, Q2);
  and and_2 (and_2_out, not_3_out, not_4_out);
  not not_4 (not_4_out, Q1);
  not not_5 (not_5_out, Q3);
  and and_3 (and_3_out, not_5_out, not_6_out, Q0);
  not not_6 (not_6_out, Q2);
  and and_4 (and_4_out, Q3, not_7_out);
  not not_7 (not_7_out, Q0);
  not not_8 (not_8_out, Q2);
  and and_5 (and_5_out, not_8_out, not_9_out);
  not not_9 (not_9_out, Q1);
  not not_10 (not_10_out, Q2);
  and and_6 (and_6_out, not_10_out, Q0);
  and and_7 (and_7_out, Q2, Q1, not_11_out);
  not not_11 (not_11_out, Q0);
  not not_12 (not_12_out, Q1);
  and and_8 (and_8_out, not_12_out, not_13_out);
  not not_13 (not_13_out, Q0);
  not not_14 (not_14_out, Q3);
  and and_9 (and_9_out, not_14_out, Q1, Q0);
  not not_15 (not_15_out, Q3);
  and and_10 (and_10_out, not_15_out, Q2);
  and and_11 (and_11_out, Q3, not_16_out);
  not not_16 (not_16_out, Q2);
  and and_12 (and_12_out, Q3, not_17_out);
  not not_17 (not_17_out, Q0);
  not not_18 (not_18_out, Q3);
  and and_13 (and_13_out, not_18_out, not_19_out);
  not not_19 (not_19_out, Q2);
  not not_20 (not_20_out, Q2);
  and and_14 (and_14_out, not_20_out, not_21_out);
  not not_21 (not_21_out, Q1);
  not not_22 (not_22_out, Q3);
  not not_23 (not_23_out, Q1);
  and and_15 (and_15_out, not_22_out, not_23_out, Q0);
  and and_16 (and_16_out, Q1, not_24_out);
  not not_24 (not_24_out, Q0);
  and and_17 (and_17_out, Q3, not_25_out);
  not not_25 (not_25_out, Q0);
  and and_18 (and_18_out, Q3, Q2, Q1);
  or or_1 (D3, and_1_out, and_2_out, and_3_out, and_4_out);
  or or_2 (D2, and_5_out, and_6_out, and_7_out, Q3);
  or or_3 (D1, and_8_out, and_9_out, and_10_out, and_11_out, and_12_out);
  or or_4 (D0, and_13_out, and_14_out, and_15_out, and_16_out, and_17_out, and_18_out);

  // Notes on the sheet:
  //   15-5-11-6-7-2-1-13-4-10
endmodule

module sequencia_guilherme (
  input  CLK,
  input  clear,
  output Q3,
  output Q2,
  output Q1,
  output Q0,
  output clk_comparador
);

  wire controle2_1_d0, controle2_1_d1, controle2_1_d2, controle2_1_d3;

  D_Flip_Flop d_ff_1 (.clk(CLK), .D(controle2_1_d3), .Q(Q3), .reset(clear));  // open: Qn, preset, en
  D_Flip_Flop d_ff_2 (.clk(CLK), .D(controle2_1_d2), .Q(Q2), .reset(clear));  // open: Qn, preset, en
  D_Flip_Flop d_ff_3 (.clk(CLK), .D(controle2_1_d1), .Q(Q1), .reset(clear));  // open: Qn, preset, en
  controle2 controle2_1 (
    .Q3(Q3), .Q2(Q2), .Q1(Q1), .Q0(Q0), .D3(controle2_1_d3), .D2(controle2_1_d2), .D1(controle2_1_d1),
    .D0(controle2_1_d0));
  D_Flip_Flop d_ff_4 (.clk(CLK), .D(controle2_1_d0), .Q(Q0), .reset(clear));  // open: Qn, preset, en
  Hex_Digit_Display hex_digit_display_1 (.value({Q3, Q2, Q1, Q0}));  // open: dp
  nor nor_1 (clk_comparador, ~Q3, Q2, ~Q1, Q0);  // NOR_Gate

  // Notes on the sheet:
  //   15-5-11-6-7-2-1-13-4-10
endmodule
